// Logisim project Divisor.circ as structural Verilog: 1 circuit, main circuit main
module main (
  input  Reset
);

  wire clock_1_out, comparator_1_eq, comparator_1_gt, comparator_1_lt, not_1_out, or_1_out;
  wire [3:0] B_p1;
  wire [7:0] A_p1, counter_1_q, multiplexer_1_out, register_1_q, subtractor_1_out;

  // DipSwitch A: pin names not known; wires that end beside it: A_p1[0], A_p1[1], A_p1[2], A_p1[3], A_p1[4], A_p1[5], A_p1[6], A_p1[7]
  not not_1 (not_1_out, Reset);
  // DipSwitch #(.number(4)) B: pin names not known; wires that end beside it: B_p1[0], B_p1[1], B_p1[2], B_p1[3]
  Subtractor subtractor_1 (.a(register_1_q), .b({4'b0000, B_p1}), .out(subtractor_1_out));  // open: bin, bout
  Comparator #(.mode("unsigned")) comparator_1 (
    .a(register_1_q), .b({4'b0000, B_p1}), .gt(comparator_1_gt), .eq(comparator_1_eq), .lt(comparator_1_lt));
  Multiplexer #(.width(8)) multiplexer_1 (.in0(A_p1), .in1(subtractor_1_out), .out(multiplexer_1_out), .sel(Reset));
  Clock clock_1 (.out(clock_1_out));
  or or_1 (or_1_out, comparator_1_gt, not_1_out, comparator_1_eq);
  Register register_1 (.D(multiplexer_1_out), .en(or_1_out), .clk(clock_1_out), .Q(register_1_q));  // open: clr
  Counter counter_1 (
    .clr(not_1_out), .up(or_1_out), .count(or_1_out), .clk(clock_1_out), .Q(counter_1_q));  // open: load, D, carry
  // LedBar #(.inputtype("row"), .matrixcols(1)) ledbar_1: pin names not known; wires that end beside it: comparator_1_lt
  // LedBar #(.inputtype("row")) ledbar_2: pin names not known; wires that end beside it: register_1_q
  // LedBar #(.inputtype("row")) ledbar_3: pin names not known; wires that end beside it: counter_1_q

  // Notes on the sheet:
  //   Dividend
  //   Divisor
  //   Remainder
  //   Quotient
  //   Counter
  //   Completed
endmodule
