// Logisim project MUX AdderSubtractor.circ as structural Verilog: 1 circuit, main circuit main
module main (
);

  wire B_p5;
  wire [1:0] M_p2;
  wire [3:0] A_p1, B_p1;
  wire [7:0] adder_1_out, adder_2_out, adder_3_out, multiplexer_1_out, multiplier_1_out, multiplier_2_out,
       subtractor_1_out;

  // DipSwitch #(.number(4)) A: pin names not known; wires that end beside it: A_p1[0], A_p1[1], A_p1[2], A_p1[3], 1'b0
  // DipSwitch #(.number(4)) B: pin names not known; wires that end beside it: B_p1[0], B_p1[1], B_p1[2], B_p1[3], B_p5, B_p5
  Multiplier multiplier_1 (.a({4'b0000, B_p1}), .b(8'h2), .out(multiplier_1_out));  // open: cin, cout
  Subtractor subtractor_1 (.a({4'b0000, A_p1}), .b(multiplier_1_out), .out(subtractor_1_out));  // open: bin, bout
  Adder adder_1 (.a({4'b0000, A_p1}), .b(multiplier_2_out), .out(adder_1_out));  // open: cin, cout
  Adder adder_2 (.a({4'b0000, A_p1}), .b({4'b0000, B_p1}), .out(adder_2_out));  // open: cin, cout
  Adder adder_3 (.a({4'b0000, A_p1}), .b(8'h1), .out(adder_3_out));  // open: cin, cout
  Multiplier multiplier_2 (.a({4'b0000, B_p1}), .b(8'h4), .out(multiplier_2_out));  // open: cin, cout
  Multiplexer #(.select(2), .width(8)) multiplexer_1 (
    .in0(subtractor_1_out), .in1(adder_1_out), .in2(adder_2_out), .in3(adder_3_out), .out(multiplexer_1_out),
    .sel(M_p2));
  // LedBar #(.inputtype("row")) ledbar_1: pin names not known; wires that end beside it: multiplexer_1_out
  // DipSwitch #(.number(2)) M: pin names not known; wires that end beside it: M_p2[1], M_p2[0]

  // Notes on the sheet:
  //   1
  //   A - 2B
  //   A + 4B
  //   A + B
  //   A + 1
  //   2
  //   4
endmodule
