// Logisim project RNG.circ as structural Verilog: 1 circuit, main circuit main
module main (
);

  wire and_1_out, and_2_out, and_3_out, and_4_out, and_5_out, and_6_out, and_7_out, and_8_out, and_9_out,
       button_1_out, button_2_out, d_ff_1_q, d_ff_1_qn, d_ff_2_q, d_ff_2_qn, ledbar_3_p1, not_1_out,
       not_2_out, not_3_out, not_4_out, not_5_out, not_6_out, not_7_out, xnor_1_out, xnor_2_out, xnor_3_out,
       xnor_4_out, xnor_5_out;
  wire [3:0] counter_1_q;
  wire [4:0] dipswitch_1_sw5, random_1_out, register_1_q, register_2_q;

  Button button_1 (.out(button_1_out));
  DipSwitch #(.number(5)) dipswitch_1 (
    .sw1(dipswitch_1_sw5[4]), .sw2(dipswitch_1_sw5[3]), .sw3(dipswitch_1_sw5[2]), .sw4(dipswitch_1_sw5[1]),
    .sw5(dipswitch_1_sw5[0]));
  and and_1 (and_1_out, d_ff_2_q, d_ff_1_q);
  D_Flip_Flop d_ff_1 (.D(d_ff_1_qn), .clk(button_2_out), .Q(d_ff_1_q), .Qn(d_ff_1_qn));  // open: preset, reset
  Button button_2 (.out(button_2_out));
  Random #(.width(5)) random_1 (.next(1'b1), .clk(button_1_out), .out(random_1_out));  // open: clr
  Register #(.width(5)) register_1 (.D(random_1_out), .en(1'b1), .clk(button_1_out), .Q(register_1_q));  // open: clr
  Register #(.width(5)) register_2 (
    .D(dipswitch_1_sw5), .en(1'b1), .clk(and_1_out), .Q(register_2_q), .clr(button_1_out));
  D_Flip_Flop d_ff_2 (.D(d_ff_2_qn), .clk(d_ff_1_qn), .Q(d_ff_2_q), .Qn(d_ff_2_qn));  // open: preset, reset
  // LedBar #(.inputtype("row"), .matrixcols(5)) ledbar_1: pin names not known; wires that end beside it: register_1_q
  xnor xnor_1 (xnor_1_out, register_1_q[0], register_2_q[0]);
  xnor xnor_2 (xnor_2_out, register_1_q[1], register_2_q[1]);
  xnor xnor_3 (xnor_3_out, register_1_q[2], register_2_q[2]);
  xnor xnor_4 (xnor_4_out, register_1_q[3], register_2_q[3]);
  xnor xnor_5 (xnor_5_out, register_1_q[4], register_2_q[4]);
  and and_2 (and_2_out, xnor_5_out, xnor_4_out);
  and and_3 (and_3_out, xnor_5_out, xnor_3_out, not_1_out);
  not not_1 (not_1_out, xnor_2_out);
  and and_4 (and_4_out, xnor_5_out, xnor_2_out, not_2_out);
  not not_2 (not_2_out, xnor_1_out);
  and and_5 (and_5_out, xnor_4_out, xnor_3_out, not_3_out);
  not not_3 (not_3_out, xnor_2_out);
  and and_6 (and_6_out, xnor_4_out, xnor_2_out, not_4_out);
  not not_4 (not_4_out, xnor_1_out);
  and and_7 (and_7_out, xnor_3_out, xnor_2_out, not_5_out);
  not not_5 (not_5_out, xnor_1_out);
  not not_6 (not_6_out, and_8_out);
  and and_8 (and_8_out, xnor_1_out, xnor_2_out, xnor_3_out, xnor_4_out, xnor_5_out);
  // LedBar #(.inputtype("row"), .matrixcols(1)) ledbar_2: pin names not known; wires that end beside it: and_8_out
  // LedBar #(.inputtype("row"), .matrixcols(1)) ledbar_3: pin names not known; wires that end beside it: ledbar_3_p1
  not not_7 (not_7_out, ledbar_3_p1);
  // LedBar #(.inputtype("row"), .matrixcols(1)) ledbar_4: pin names not known; wires that end beside it: not_7_out
  or or_1 (ledbar_3_p1, and_2_out, and_3_out, and_4_out, and_5_out, and_6_out, and_7_out);
  Counter #(.max('hf), .width(4)) counter_1 (
    .clr(button_1_out), .up(1'b1), .count(1'b1), .clk(and_9_out), .Q(counter_1_q));  // open: load, D, carry
  and and_9 (and_9_out, and_1_out, not_6_out);
  // LedBar #(.inputtype("row"), .matrixcols(4)) ledbar_5: pin names not known; wires that end beside it: counter_1_q

  // Notes on the sheet:
  //   GRN
  //   User input
  //   Clk
  //   Sends output of 1 every 4 ticks
  //   Random
  //   Correct Answer
  //   High
  //   Low
  //   Counter
endmodule
