// Logisim project SRingShifter.circ as structural Verilog: 1 circuit, main circuit main
module main (
);

  wire button_1_out, button_2_out, button_3_out, button_4_out, button_5_out, button_6_out, d_ff_1_q,
       d_ff_2_q, d_ff_3_q, d_ff_4_q, multiplexer_1_out, not_1_out;

  Button button_1 (.out(button_1_out));
  Button button_2 (.out(button_2_out));
  Button button_3 (.out(button_3_out));
  Button button_4 (.out(button_4_out));
  Button button_5 (.out(button_5_out));
  Button button_6 (.out(button_6_out));
  D_Flip_Flop d_ff_1 (
    .D(multiplexer_1_out), .clk(button_6_out), .Q(d_ff_1_q), .preset(button_4_out), .reset(button_5_out));  // open: Qn
  D_Flip_Flop d_ff_2 (
    .D(d_ff_1_q), .clk(button_6_out), .Q(d_ff_2_q), .preset(button_3_out), .reset(button_5_out));  // open: Qn
  D_Flip_Flop d_ff_3 (
    .D(d_ff_2_q), .clk(button_6_out), .Q(d_ff_3_q), .preset(button_2_out), .reset(button_5_out));  // open: Qn
  D_Flip_Flop d_ff_4 (
    .D(d_ff_3_q), .clk(button_6_out), .Q(d_ff_4_q), .preset(button_1_out), .reset(button_5_out));  // open: Qn
  not not_1 (not_1_out, d_ff_4_q);
  Multiplexer multiplexer_1 (.in0(d_ff_4_q), .in1(not_1_out), .out(multiplexer_1_out), .sel(d_ff_4_q));

  // Notes on the sheet:
  //   S
  //   R
  //   Clk
endmodule
